# Fritzing sketch VoiTux v2.0 Vue d'ensemble (saved by Fritzing 0.9.3b)

parts:
  Raspberry_Pi1 = Raspberry Pi B rev2
  S1 = H-Bridge with L298N
  M1 = DC Motor
  J1 = Basic Servo
  BAT1 = BC9VPC [package=bc9vpc]
  U1 = TRANSCHIPTC5747 [package=camera_sfv24r-2st_2]  # not connected

nets:
  GND: Raspberry_Pi1.GND, S1.GND, J1.gnd
  N1: Raspberry_Pi1.GPIO_27, S1.IN3
  N2: Raspberry_Pi1.GPIO_22, S1.IN4
  N3: Raspberry_Pi1.GPIO_4, J1.pulse
  N4: S1.12V, BAT1.V+
  5V: S1.5V, J1.vcc
  N5: S1.OUT3-Motor2, M1.pin_2
  N6: S1.OUT4-Motor2, M1.pin_1

custom parts:
  H-Bridge with L298N: h-bridge
